// Logisim project cpuV0.circ as structural Verilog: 8 circuits, main circuit main
module ULA (
  input  [7:0] A,
  input  [7:0] B,
  input  OP,
  output overflow__sem_sinal,
  output overflow__com_sinal,
  output O,
  output O_2,
  output O_3,
  output [7:0] R
);

  wire somador_1_c7, somador_1_c8;
  wire [7:0] xor_1_out;

  assign xor_1_out = {8{OP}} ^ B;  // XOR_Gate xor_1, 8 bits wide
  Somador somador_1 (.c0(OP), .A(A), .B(xor_1_out), .S(R), .c7(somador_1_c7), .c8(somador_1_c8));
  Comparador comparador_1 (.A(A), .B(B), .O(O), .O_2(O_2), .O_3(O_3));
  xor xor_2 (overflow__sem_sinal, OP, somador_1_c8);
  xor xor_3 (overflow__com_sinal, somador_1_c8, somador_1_c7);

  // Notes on the sheet:
  //   c0 = OP
  //   Circuito ULA: Recebe dois operandos de 8 bits (A e B), e um bit OP (0 para adição e 1 para subtração) e devolve R (o resultado
  //   da operação entre A e B), e outros 5 bits que indicam se houve overflow na interpretação sem sinal, se houve overflow na interpretação
  //   com sinal, se A = B, se A > B ou A < B
  //   inverte B se OP = 1
  //   somador
  //   Comparador
  //   c8 xor OP
  //   c8 xor c7
  //   indica se A = B
  //   indica se A > B
  //   indica se A < B
endmodule

module Somador (
  input  [7:0] A,
  input  [7:0] B,
  input  c0,
  output c7,
  output c8,
  output [7:0] S
);

  wire somabits_1_cout, somabits_2_cout, somabits_3_cout, somabits_4_cout, somabits_5_cout, somabits_6_cout;

  Somabits somabits_1 (.Cin(somabits_2_cout), .a(A[1]), .b(B[1]), .S(S[1]), .Cout(somabits_1_cout));
  Somabits somabits_2 (.Cin(c0), .a(A[0]), .b(B[0]), .S(S[0]), .Cout(somabits_2_cout));
  Somabits somabits_3 (.Cin(somabits_1_cout), .a(A[2]), .b(B[2]), .S(S[2]), .Cout(somabits_3_cout));
  Somabits somabits_4 (.Cin(somabits_5_cout), .a(A[4]), .b(B[4]), .S(S[4]), .Cout(somabits_4_cout));
  Somabits somabits_5 (.Cin(somabits_3_cout), .a(A[3]), .b(B[3]), .S(S[3]), .Cout(somabits_5_cout));
  Somabits somabits_6 (.Cin(somabits_4_cout), .a(A[5]), .b(B[5]), .S(S[5]), .Cout(somabits_6_cout));
  Somabits somabits_7 (.Cin(c7), .a(A[7]), .b(B[7]), .S(S[7]), .Cout(c8));
  Somabits somabits_8 (.Cin(somabits_6_cout), .a(A[6]), .b(B[6]), .S(S[6]), .Cout(c7));

  // Notes on the sheet:
  //   e devolve S = A + B se OP = 0
  //   ou devolve S = A - B se OP = 1
  //   também devolve os bits c7 e c8, que são os valores dos dois últimos carrys da operação
  //   Circuito Somador: recebe dois operandos de oito bits (A e B) e um bit OP
  //   <- somabits
endmodule

module Somabits (
  input  a,
  input  b,
  input  Cin,
  output Cout,
  output S
);

  wire and_1_out, and_2_out, xor_1_out;

  xor xor_1 (xor_1_out, a, b);
  xor xor_2 (S, Cin, xor_1_out);
  and and_1 (and_1_out, a, b);
  or or_1 (Cout, and_1_out, and_2_out);
  and and_2 (and_2_out, xor_1_out, Cin);

  // Notes on the sheet:
  //   Circuito somabits: Recebe três bits (a, b e Cin) e devolve
  //   S = (a xor b) xor Cin       e    Cout = [(a xor b)and Cin] or Cout
endmodule

module Comparador (
  input  [7:0] A,
  input  [7:0] B,
  output O,
  output O_2,
  output O_3
);

  wire compara4bits_1_o, compara4bits_1_o_2, compara4bits_1_o_3, compara4bits_2_o_2, compara4bits_2_o_3;

  Compara4bits compara4bits_1 (
    .i(1'b1), .A(A[7:4]), .B(B[7:4]), .O(compara4bits_1_o), .O_2(compara4bits_1_o_2), .O_3(compara4bits_1_o_3));
  Compara4bits compara4bits_2 (
    .i(compara4bits_1_o), .A(A[3:0]), .B(B[3:0]), .O(O), .O_2(compara4bits_2_o_2), .O_3(compara4bits_2_o_3));
  xor xor_1 (O_2, compara4bits_2_o_2, compara4bits_1_o_2);
  xor xor_2 (O_3, compara4bits_2_o_3, compara4bits_1_o_3);

  // Notes on the sheet:
  //   Compara4bits
  //   Compara4bits
  //   Comparador foi implementado com 2 Compara4bits. O primeiro compara A7A6A5A4 com B7B6B5B4, o segundo
  //   para O> se A > B ou 1 para O< se A < B ( apenas uma das três saídas recebe 1, as outras recebem 0).
  //   As comparações são referentes a interpretação sem sinal.
  //   compara A3A2A1A0 com B3B2B1B0
  //   Circuito Compara4bits: Recebe um bit i e 2 números de 4 bits ( A e B) e devolve outros 3 bits ( O=, O< e O>). Se i =1, devolve 1 para O= se A = B ou 1
endmodule

// AC
module main (
  input  Inc,
  input  reset_PC,
  input  Write_0_read_1,
  input  [7:0] in_4,
  input  _0_AC_1_IR
);

  wire _1, _3, clk, decoder_1_out1, decoder_1_out2;
  wire [7:0] AC_q, controlled_buffer_1_out, controlled_inverter_2_out, IR_q, IR_q_2, PC_q;
  wire [15:0] controlled_inverter_1_out, dest1, ram_1_data;

  Clock clock_1 (.out(clk));
  Counter PC (.count(Inc), .Q(PC_q), .clk(clk), .clr(reset_PC));  // open: load, D, carry
  Hex_Digit_Display hex_digit_display_1 (.value(dest1[11:8]));  // open: dp
  Hex_Digit_Display hex_digit_display_2 (.value(dest1[15:12]));  // open: dp
  assign controlled_buffer_1_out = _3 ? PC_q : 8'bz;  // Controlled_Buffer controlled_buffer_1
  Hex_Digit_Display hex_digit_display_3 (.value(dest1[7:4]));  // open: dp
  assign controlled_buffer_1_out = _1 ? IR_q : 8'bz;  // Controlled_Buffer controlled_buffer_2
  Hex_Digit_Display hex_digit_display_4 (.value(dest1[3:0]));  // open: dp
  Register #(.width(16)) IR (.D(controlled_inverter_1_out), .Q({IR_q_2, IR_q}), .clk(clk));  // open: en, clr
  Decoder #(.select(2)) decoder_1 (
    .out1(decoder_1_out1), .out2(decoder_1_out2), .sel(IR_q_2[1:0]));  // open: out0, out3, en
  assign controlled_inverter_1_out = _1 ? ~ram_1_data : 16'bz;  // Controlled_Inverter controlled_inverter_1
  RAM #(.dataWidth(16)) ram_1 (
    .addr(controlled_buffer_1_out), .data(ram_1_data), .sel(clk), .ld(_1));  // open: clk, clr
  assign controlled_inverter_2_out = _1 ? ~ram_1_data[7:0] : 8'bz;  // Controlled_Inverter controlled_inverter_2
  Register AC (.D(controlled_inverter_2_out), .Q(AC_q), .clk(clk));  // open: en, clr
  assign ram_1_data[7:0] = _1 ? AC_q : 8'bz;  // Controlled_Buffer controlled_buffer_3
  not not_1 (_1, _1);
  assign _1 = decoder_1_out1 ? 1'b1 : 1'bz;  // Controlled_Buffer controlled_buffer_4
  not not_2 (_3, _1);
  not not_3 (_1, _1);
  assign _1 = decoder_1_out2 ? 1'b1 : 1'bz;  // Controlled_Buffer controlled_buffer_5
  not not_4 (_3, _1);
  // also tied to GND on the sheet: {ram_1_data[8], ram_1_data[9], ram_1_data[10], ram_1_data[11], ram_1_data[12], ram_1_data[13], ram_1_data[14], ram_1_data[15]}

  // Other names for the same wires on the sheet: _2 = _1; _4 = _1

  // Notes on the sheet:
  //   João Seckler, 4603521, joaoseckler@gmail.com
  //   Jose Eduardo R M Peres y Peres, 8945332, jose.peres@usp.br
  //   Gilvane da Silva Sousa, 10258726, gilvane.silva1@usp.br
  //   Read/write
  //   Parte 3: cpu V zero
  //   0x01EE
  //   0x02EE
  //   FLAGS
  //   1. 0=RAM addr -> IR/1= IR -> RAM addr
  //   2. 0=RAM -> AC/1 = AC -> RAM
  //   3. 0= PC -/-> RAM/1= PC -> RAM
  //   4. RAM 0=read/1=write
  //   2
endmodule

module Comparabits (
  input  i,
  input  a,
  input  b,
  output O,
  output O_2,
  output O_3
);

  wire not_1_out, not_2_out, xnor_1_out;

  xnor xnor_1 (xnor_1_out, a, b);
  and and_1 (O_2, a, i, not_1_out);
  not not_1 (not_1_out, b);
  not not_2 (not_2_out, a);
  and and_2 (O_3, not_2_out, i, b);
  and and_3 (O, i, xnor_1_out);

  // Notes on the sheet:
  //   Circuito Comparabits: Recebe 3 bits ( a, b e i) e devolve outros 3 bits ( O=, O< e O>). Se i =1, devolve 1 para O= se a = b ou 1
  //   para O> se a > b ou 1 para O< se a < b ( apenas uma das três saídas recebe 1, as outras recebem 0).
  //   Também, se i=0, não compara os bits a e b, devolve 0 nas três saídas. As comparações são referentes a interpretação sem sinal.
  //   i AND ( a XNOR b)
  //   a AND ( NOT b)
  //   (NOT a) AND b
endmodule

module Compara2bits (
  input  [1:0] A,
  input  [1:0] B,
  input  i,
  output O,
  output O_2,
  output O_3
);

  wire comparabits_1_o, comparabits_1_o_2, comparabits_1_o_3, comparabits_2_o_2, comparabits_2_o_3;

  Comparabits comparabits_1 (
    .i(i), .a(A[1]), .b(B[1]), .O(comparabits_1_o), .O_2(comparabits_1_o_2), .O_3(comparabits_1_o_3));
  Comparabits comparabits_2 (
    .i(comparabits_1_o), .a(A[0]), .b(B[0]), .O(O), .O_2(comparabits_2_o_2), .O_3(comparabits_2_o_3));
  or or_1 (O_2, comparabits_2_o_2, comparabits_1_o_2);
  or or_2 (O_3, comparabits_2_o_3, comparabits_1_o_3);

  // Notes on the sheet:
  //   Comparabits
  //   Comparabits
  //   Compara2bits foi implementado com 2 Comparabits. O primeiro compara A1 e B1, o segundo compara A0 e B0.
  //   para O> se A > B ou 1 para O< se A < B ( apenas uma das três saídas recebe 1, as outras recebem 0).
  //   Também, se i=0, não compara A e B, devolve 0 nas três saídas. As comparações são referentes a interpretação sem sinal.
  //   Circuito Compara2bits: Recebe um bit i e 2 números de 2 bits ( A e B) e devolve outros 3 bits ( O=, O< e O>). Se i =1, devolve 1 para O= se A = B ou 1
  //   A = B
  //   A > B
  //   A < B
endmodule

module Compara4bits (
  input  [3:0] A,
  input  [3:0] B,
  input  i,
  output O,
  output O_2,
  output O_3
);

  wire compara2bits_1_o, compara2bits_1_o_2, compara2bits_1_o_3, compara2bits_2_o_2, compara2bits_2_o_3;

  Compara2bits compara2bits_1 (
    .i(i), .A(A[3:2]), .B(B[3:2]), .O(compara2bits_1_o), .O_2(compara2bits_1_o_2), .O_3(compara2bits_1_o_3));
  Compara2bits compara2bits_2 (
    .i(compara2bits_1_o), .A(A[1:0]), .B(B[1:0]), .O(O), .O_2(compara2bits_2_o_2), .O_3(compara2bits_2_o_3));
  or or_1 (O_2, compara2bits_2_o_2, compara2bits_1_o_2);
  or or_2 (O_3, compara2bits_2_o_3, compara2bits_1_o_3);

  // Notes on the sheet:
  //   Compara2bits
  //   Compara2bits
  //   para O> se A > B ou 1 para O< se A < B ( apenas uma das três saídas recebe 1, as outras recebem 0).
  //   Também, se i=0, não compara A e B, devolve 0 nas três saídas. As comparações são referentes a interpretação sem sinal.
  //   Compara4bits foi implementado com 2 Compara2bits. O primeiro compara A3A2 com B3B2, o segundo compara A1A0 com B1B0.
  //   Circuito Compara4bits: Recebe um bit i e 2 números de 4 bits ( A e B) e devolve outros 3 bits ( O=, O< e O>). Se i =1, devolve 1 para O= se A = B ou 1
  //   A = B
  //   A > B
  //   A < B
endmodule
