// Logisim project somador.circ as structural Verilog: 3 circuits, main circuit main
module main (
  input  [7:0] A,
  input  [7:0] B,
  input  OP,
  output overflow__sem_sinal,
  output overflow__com_sinal,
  output [7:0] R
);

  wire somador_c7, somador_c8;
  wire [7:0] xor_1_out;

  xor xor_1 (xor_1_out[0], B[0], OP);
  xor xor_2 (xor_1_out[1], B[1], OP);
  xor xor_3 (xor_1_out[2], B[2], OP);
  xor xor_4 (xor_1_out[3], B[3], OP);
  xor xor_5 (xor_1_out[4], B[4], OP);
  xor xor_6 (xor_1_out[5], B[5], OP);
  xor xor_7 (xor_1_out[6], B[6], OP);
  xor xor_8 (xor_1_out[7], B[7], OP);
  somador somador (.c0(OP), .A(A), .B(xor_1_out), .S(R), .c7(somador_c7), .c8(somador_c8));
  xor xor_9 (overflow__sem_sinal, OP, somador_c8);
  xor xor_10 (overflow__com_sinal, somador_c7, somador_c8);

  // Notes on the sheet:
  //   João Seckler, 4603521, joaoseckler@gmail.com
  //   Jose Eduardo R M Peres y Peres, 8945332, jose.peres@usp.br
  //   Parte 1: Circuito Somador
  //   Circuito para adição e subtração de números de 8 bits
endmodule

module somador (
  input  [7:0] A,
  input  [7:0] B,
  input  c0,
  output c7,
  output c8,
  output [7:0] S
);

  wire somabits_1_cout, somabits_2_cout, somabits_3_cout, somabits_4_cout, somabits_5_cout, somabits_6_cout;

  somabits somabits_1 (.Cin(c0), .x(A[0]), .y(A[0]), .S(S[0]), .Cout(somabits_1_cout));
  somabits somabits_2 (.Cin(somabits_1_cout), .x(A[1]), .y(B[1]), .S(S[1]), .Cout(somabits_2_cout));
  somabits somabits_3 (.Cin(somabits_2_cout), .x(A[2]), .y(B[2]), .S(S[2]), .Cout(somabits_3_cout));
  somabits somabits_4 (.Cin(somabits_5_cout), .x(A[4]), .y(B[4]), .S(S[4]), .Cout(somabits_4_cout));
  somabits somabits_5 (.Cin(somabits_3_cout), .x(A[3]), .y(B[3]), .S(S[3]), .Cout(somabits_5_cout));
  somabits somabits_6 (.Cin(somabits_4_cout), .x(A[5]), .y(B[5]), .S(S[5]), .Cout(somabits_6_cout));
  somabits somabits_7 (.Cin(c7), .x(A[7]), .y(B[7]), .S(S[7]), .Cout(c8));
  somabits somabits_8 (.Cin(somabits_6_cout), .x(A[6]), .y(B[6]), .S(S[6]), .Cout(c7));

  assign B[0] = A[0];
endmodule

module somabits (
  input  x,
  input  y,
  input  Cin,
  output Cout,
  output S
);

  wire and_1_out, and_2_out, xor_1_out;

  xor xor_1 (xor_1_out, x, y);
  xor xor_2 (S, Cin, xor_1_out);
  and and_1 (and_1_out, y, x);
  or or_1 (Cout, and_1_out, and_2_out);
  and and_2 (and_2_out, xor_1_out, Cin);
endmodule
