// Logisim project ula.circ as structural Verilog: 6 circuits, main circuit main
module ULA (
  input  [7:0] A,
  input  [7:0] B,
  input  OP,
  output overflow__sem_sinal,
  output overflow__com_sinal,
  output o,
  output _0,
  output o_2,
  output [7:0] R
);

  wire somador_1_c7, somador_1_c8;
  wire [7:0] xor_1_out;

  assign xor_1_out = {8{OP}} ^ B;  // XOR_Gate xor_1, 8 bits wide
  Somador somador_1 (.c0(OP), .A(A), .B(xor_1_out), .S(R), .c7(somador_1_c7), .c8(somador_1_c8));
  Comparador comparador_1 (.A(A), .B(B), .o(o), .o_2(_0), .o_3(o_2));
  xor xor_2 (overflow__sem_sinal, OP, somador_1_c8);
  xor xor_3 (overflow__com_sinal, somador_1_c8, somador_1_c7);

  // Notes on the sheet:
  //   inverte B se OP = 1
  //   somador
  //   c8 xor OP
  //   c8 xor c7
endmodule

module Somador (
  input  [7:0] A,
  input  [7:0] B,
  input  c0,
  output c7,
  output c8,
  output [7:0] S
);

  wire somabits_1_cout, somabits_2_cout, somabits_3_cout, somabits_4_cout, somabits_5_cout, somabits_6_cout;

  Somabits somabits_1 (.Cin(somabits_2_cout), .a(A[1]), .b(B[1]), .S(S[1]), .Cout(somabits_1_cout));
  Somabits somabits_2 (.Cin(c0), .a(A[0]), .b(B[0]), .S(S[0]), .Cout(somabits_2_cout));
  Somabits somabits_3 (.Cin(somabits_1_cout), .a(A[2]), .b(B[2]), .S(S[2]), .Cout(somabits_3_cout));
  Somabits somabits_4 (.Cin(somabits_5_cout), .a(A[4]), .b(B[4]), .S(S[4]), .Cout(somabits_4_cout));
  Somabits somabits_5 (.Cin(somabits_3_cout), .a(A[3]), .b(B[3]), .S(S[3]), .Cout(somabits_5_cout));
  Somabits somabits_6 (.Cin(somabits_4_cout), .a(A[5]), .b(B[5]), .S(S[5]), .Cout(somabits_6_cout));
  Somabits somabits_7 (.Cin(c7), .a(A[7]), .b(B[7]), .S(S[7]), .Cout(c8));
  Somabits somabits_8 (.Cin(somabits_6_cout), .a(A[6]), .b(B[6]), .S(S[6]), .Cout(c7));

  // Notes on the sheet:
  //   e devolve S = A + B se OP = 0
  //   ou devolve S = A - B se OP = 1
  //   também devolve os bits c7 e c8, que são os valores dos dois últimos carrys da operação
  //   Circuito Somador: recebe dois operandos de oito bits (A e B) e um bit OP
  //   <- somabits
endmodule

module Somabits (
  input  a,
  input  b,
  input  Cin,
  output Cout,
  output S
);

  wire and_1_out, and_2_out, xor_1_out;

  xor xor_1 (xor_1_out, a, b);
  xor xor_2 (S, Cin, xor_1_out);
  and and_1 (and_1_out, a, b);
  or or_1 (Cout, and_1_out, and_2_out);
  and and_2 (and_2_out, xor_1_out, Cin);

  // Notes on the sheet:
  //   Circuito somabits: Recebe três bits (a, b e Cin) e devolve
  //   S = (a xor b) xor Cin       e    Cout = [(a xor b)and Cin] or Cout
endmodule

module Comparador (
  input  [7:0] A,
  input  [7:0] B,
  output o,
  output o_2,
  output o_3
);

  wire comparabits_1_a_b, comparabits_1_a_b_2, comparabits_1_out_4, comparabits_2_a_b, comparabits_2_a_b_2,
       comparabits_2_out_4, comparabits_3_a_b, comparabits_3_a_b_2, comparabits_3_out_4, comparabits_4_a_b,
       comparabits_4_a_b_2, comparabits_4_out_4, comparabits_5_a_b, comparabits_5_a_b_2, comparabits_5_out_4,
       comparabits_6_a_b, comparabits_6_a_b_2, comparabits_6_out_4, comparabits_7_a_b, comparabits_7_a_b_2,
       comparabits_7_out_4, comparabits_8_a_b, comparabits_8_a_b_2;

  Comparabits comparabits_1 (
    .i(1'b1), .a(A[7]), .b(B[7]), .out_4(comparabits_1_out_4), .a_b(comparabits_1_a_b),
    .a_b_2(comparabits_1_a_b_2));
  Comparabits comparabits_2 (
    .i(comparabits_1_out_4), .a(A[6]), .b(B[6]), .out_4(comparabits_2_out_4), .a_b(comparabits_2_a_b),
    .a_b_2(comparabits_2_a_b_2));
  or or_1 (o_3, comparabits_1_a_b_2, comparabits_2_a_b_2, comparabits_3_a_b_2, comparabits_4_a_b_2, comparabits_5_a_b_2, comparabits_6_a_b_2, comparabits_7_a_b_2, comparabits_8_a_b_2);
  Comparabits comparabits_3 (
    .i(comparabits_2_out_4), .a(A[5]), .b(B[5]), .out_4(comparabits_3_out_4), .a_b(comparabits_3_a_b),
    .a_b_2(comparabits_3_a_b_2));
  Comparabits comparabits_4 (
    .i(comparabits_3_out_4), .a(A[4]), .b(B[4]), .out_4(comparabits_4_out_4), .a_b(comparabits_4_a_b),
    .a_b_2(comparabits_4_a_b_2));
  Comparabits comparabits_5 (
    .i(comparabits_4_out_4), .a(A[3]), .b(B[3]), .out_4(comparabits_5_out_4), .a_b(comparabits_5_a_b),
    .a_b_2(comparabits_5_a_b_2));
  or or_2 (o_2, comparabits_1_a_b, comparabits_2_a_b, comparabits_3_a_b, comparabits_4_a_b, comparabits_5_a_b, comparabits_6_a_b, comparabits_7_a_b, comparabits_8_a_b);
  Comparabits comparabits_6 (
    .i(comparabits_5_out_4), .a(A[2]), .b(B[2]), .out_4(comparabits_6_out_4), .a_b(comparabits_6_a_b),
    .a_b_2(comparabits_6_a_b_2));
  Comparabits comparabits_7 (
    .i(comparabits_6_out_4), .a(A[1]), .b(B[1]), .out_4(comparabits_7_out_4), .a_b(comparabits_7_a_b),
    .a_b_2(comparabits_7_a_b_2));
  Comparabits comparabits_8 (
    .i(comparabits_7_out_4), .a(A[0]), .b(B[0]), .out_4(o), .a_b(comparabits_8_a_b),
    .a_b_2(comparabits_8_a_b_2));

  // Notes on the sheet:
  //   Circuito Comparador:
endmodule

module main (
  input  [7:0] A,
  input  [7:0] B,
  input  \Operação ,
  output overflow_com_sinal,
  output overflow_sem_sinal,
  output out_6,
  output out_7,
  output out_8
);

  ULA ula_1 (
    .OP(\Operação ), .A(A), .B(B), .overflow__sem_sinal(overflow_com_sinal),
    .overflow__com_sinal(overflow_sem_sinal), .o(out_6), ._0(out_7), .o_2(out_8));  // open: R

  // Notes on the sheet:
  //   João Seckler, 4603521, joaoseckler@gmail.com
  //   Gilvane da Silva Sousa, 10258726, gilvane.silva1@usp.br
  //   Jose Eduardo R M Peres y Peres, 8945332, jose.peres@usp.br
  //   Parte 2: ULA
  //   Unidade Lógico-Aritmética
  //   ULA
endmodule

module Comparabits (
  input  i,
  input  a,
  input  b,
  output out_4,
  output a_b,
  output a_b_2
);

  wire not_1_out, not_2_out, not_3_out, xor_1_out;

  xor xor_1 (xor_1_out, a, b);
  and and_1 (a_b, a, i, not_1_out);
  not not_1 (not_1_out, b);
  not not_2 (not_2_out, a);
  and and_2 (a_b_2, not_2_out, i, b);
  and and_3 (out_4, i, not_3_out);
  not not_3 (not_3_out, xor_1_out);

  // Notes on the sheet:
  //   Se i = 0, comparabits devolve 0 em todas as saídas
  //   Caso contrário, se comporta como um comparador de bits
endmodule
